# Fritzing sketch TruckController (saved by Fritzing 0.9.3b)
circuit board: 7.12509cm x 4.094cm

parts:
  Steering = Dagu DGServo 9g header (male) [package=THT]
  ESC = Dagu DGServo 9g header (male) [package=THT]
  Gearbox = Dagu DGServo 9g header (male) [package=THT]
  FFT1 = MOSFET-NCHANNEL [package=to220v]
  R1 = Resistor [tolerance=±5% resistance=10k package=THT]
  BackLights = male pin header, 5 pins [form="♂ (male)"]
  TrailerLights = male pin header, 5 pins [form="♂ (male)"]
  FrontLights = male pin header, 6 pins [form="♂ (male)"]
  SidePos = male pin header, 2 pins [form="♂ (male)"]
  TopPos = male pin header, 2 pins [form="♂ (male)"]
  FFT2 = MOSFET-NCHANNEL [package=to220v]
  R2 = Resistor [tolerance=±5% resistance=10k package=THT]
  FFT3 = MOSFET-NCHANNEL [package=to220v]
  FFT5 = MOSFET-NCHANNEL [package=to220v]
  FFT6 = MOSFET-NCHANNEL [package=to220v]
  FFT7 = MOSFET-NCHANNEL [package=to220v]
  R3 = Resistor [tolerance=±5% resistance=10k package=THT]
  R4 = Resistor [tolerance=±5% resistance=10k package=THT]
  R5 = Resistor [tolerance=±5% resistance=10k package=THT]
  R6 = Resistor [tolerance=±5% resistance=10k package=THT]
  R7 = Resistor [tolerance=±5% resistance=10k package=THT]
  FFT8 = MOSFET-NCHANNEL [package=to220v]
  R8 = Resistor [tolerance=±5% resistance=10k package=THT]
  RedBear_Duo = RedBear-Duo
  SideIndicators = male pin header, 3 pins [form="♂ (male)"]
  FFT4 = MOSFET-NCHANNEL [package=to220v]
  Sound = male pin header, 4 pins [form="♂ (male)"]

nets:
  GND: Steering.gnd, ESC.gnd, Gearbox.gnd, FFT1.S, R1.Pin_1, FFT2.S, R2.Pin_1, FFT3.S, FFT5.S, FFT6.S, FFT7.S, R3.Pin_1, R4.Pin_1, R5.Pin_1, R6.Pin_1, R7.Pin_1, FFT8.S, R8.Pin_1, RedBear_Duo.GND, FFT4.S, Sound.pin2
  VCC: Steering.Vcc, Gearbox.Vcc, BackLights.pin1, TrailerLights.pin1, FrontLights.pin1, SidePos.pin1, TopPos.pin1, RedBear_Duo.3V3, SideIndicators.pin1, Sound.pin1
  N1: Steering.pulse, RedBear_Duo.A4
  VCC_2: ESC.Vcc, RedBear_Duo.VIN
  N2: ESC.pulse, RedBear_Duo.DAC
  N3: Gearbox.pulse, RedBear_Duo.A5
  N4: FFT1.G, R1.Pin_0, RedBear_Duo.D6
  N5: FFT1.D, SidePos.pin2, TopPos.pin2
  N6: BackLights.pin2, TrailerLights.pin2, FFT2.D
  N7: BackLights.pin3, TrailerLights.pin3, FFT7.D
  N8: BackLights.pin4, TrailerLights.pin4, FrontLights.pin4, FFT6.D, SideIndicators.pin2
  N9: BackLights.pin5, TrailerLights.pin5, FrontLights.pin5, FFT5.D, SideIndicators.pin3
  N10: FrontLights.pin2, FFT4.D
  N11: FrontLights.pin3, FFT3.D
  N12: FrontLights.pin6, FFT8.D
  N13: FFT2.G, R2.Pin_0, RedBear_Duo.D5
  N14: FFT3.G, R3.Pin_0, RedBear_Duo.D4
  N15: FFT5.G, R5.Pin_0, RedBear_Duo.D2
  N16: FFT6.G, R6.Pin_0, RedBear_Duo.D1
  N17: FFT7.G, R7.Pin_0, RedBear_Duo.D0
  N18: R4.Pin_0, RedBear_Duo.D3, FFT4.G
  N19: FFT8.G, R8.Pin_0, RedBear_Duo.D7
  N20: RedBear_Duo.RX, Sound.pin4
  N21: RedBear_Duo.TX, Sound.pin3

notes:
  Truck Controller V1.0
  (c) Thomas Proffen, 2018
  +

custom parts:
  RedBear-Duo: Duo is a thumb-size development board made to simplify the building process of Internet of Things (IoT). This part is a modification of the Particle Photon part by Brett Walach,Fabian Althaus
